# Fritzing sketch annoy_ppl (saved by Fritzing 1.0.6)
breadboards: 2

parts:
  Part1 = Arduino Uno (Rev3) - ICSP
  M1 = gear-motor
  M2 = gear-motor
  IC1 = L293D [package=THT]
  U1 = 74HC595 SMD [package="SO16 [SMD]"]
  LED1 = RGB LED (com. cathode, rbg) [color="Red (633nm)" current=0.030A package="5 mm [THT]"]
  LED2 = RGB LED (com. cathode, rbg) [color="Red (633nm)" current=0.030A package="5 mm [THT]"]
  R1 = Resistor [tolerance=±5% power=0.25W resistance=1k package=THT]
  R2 = Resistor [tolerance=±5% power=0.25W resistance=1k package=THT]
  R3 = Resistor [tolerance=±5% power=0.25W resistance=220 package=THT]
  R4 = Resistor [tolerance=±5% power=0.25W resistance=220 package=THT]
  R5 = Resistor [tolerance=±5% power=0.25W resistance=1k package=THT]
  R6 = Resistor [tolerance=±5% power=0.25W resistance=1k package=THT]
  HC-SR04_Sensor_1 = HC-SR04 Ultrasonic Distance Sensor
  LED3 = LED - 5mm [color="White (4500K)" current=0.030A package="5 mm [THT]"]
  R7 = Resistor [tolerance=±5% power=0.25W resistance=220 package=THT]
  LED4 = LED - 5mm [color="White (4500K)" current=0.030A package="5 mm [THT]"]
  R8 = Resistor [tolerance=±5% power=0.25W resistance=220 package=THT]
  M3 = fc-51 [package=THT]
  M4 = fc-51 [package=THT]
  LED5 = LED - 5mm [color="Blue (525nm)" current=0.030A package="5 mm [THT]"]
  LED6 = LED - 5mm [color="Blue (525nm)" current=0.030A package="5 mm [THT]"]
  R9 = Resistor [tolerance=±5% power=0.25W resistance=5k package=THT]
  R10 = Resistor [tolerance=±5% power=0.25W resistance=5k package=THT]
  Mod1 = Passive Buzzer

nets:
  N1: Part1.A0, R6.Pin_1
  N2: Part1.A2, R5.Pin_1
  N3: Part1.A4/SDA, Mod1.S
  N4: Part1.A5/SCL, HC-SR04_Sensor_1.TRIG
  N5: Part1.D8, M3.pin1
  N6: Part1.D9_PWM, IC1.In_3
  N7: Part1.D10_PWM/SS, IC1.In_2
  N8: Part1.D11_PWM/MOSI, HC-SR04_Sensor_1.ECHO
  N9: Part1.D13/SCK, R9.Pin_1, R10.Pin_0
  GND: Part1.GND, U1.GND, U1.OE
  N10: Part1.D2, U1.SH_CP
  N11: Part1.D3_PWM, U1.DS
  N12: Part1.D4, U1.ST_CP
  N13: Part1.D5_PWM, IC1.In_4
  N14: Part1.D6_PWM, IC1.In_1
  N15: Part1.D7, M4.pin1
  VCC: Part1.5V, IC1.+Vmotor, U1.MR, U1.VCC, HC-SR04_Sensor_1.VCC, M3.pin3, M4.pin3
  N16: M1.pin_1, IC1.Out_3_(_Controlled_by_Enable_2_)
  N17: M1.pin_2, IC1.Out_2_(_Controlled_by_Enable_1_)
  N18: M2.pin_1, IC1.Out_1_(_Controlled_by_Enable_1_)
  N19: M2.pin_2, IC1.Out_4_(_Controlled_by_Enable_2_)
  N20: IC1.0V, LED1.common_cathode, LED2.common_cathode, HC-SR04_Sensor_1.GND, LED3.cathode, LED4.cathode, M3.pin2, M4.pin2, LED5.cathode, LED6.cathode, Mod1.-
  N21: U1.Q1, R8.Pin_1
  N22: U1.Q2, R7.Pin_1
  N23: U1.Q4, R1.Pin_1
  N24: U1.Q6, R2.Pin_1
  N25: LED1.red_anode, R1.Pin_0
  N26: LED1.blue_anode, R2.Pin_0
  N27: LED1.green_anode, R3.Pin_0
  N28: LED2.red_anode, R5.Pin_0
  N29: LED2.blue_anode, R6.Pin_0
  N30: LED2.green_anode, R4.Pin_0
  N31: LED3.anode, R7.Pin_0
  N32: LED4.anode, R8.Pin_0
  N33: LED5.anode, R9.Pin_0
